# Fritzing sketch clockers (saved by Fritzing 0.9.3b)
circuit board: 6.5cm x 3.2cm
breadboards: 1

parts:
  Motor_1 = male pin header, 4 pins [form="♂ (male)"]
  Motor_2 = male pin header, 4 pins [form="♂ (male)"]
  Motor_3 = male pin header, 4 pins [form="♂ (male)"]
  J7 = male pin header, 2 pins [form="♂ (male)"]
  +_- = male pin header, 2 pins [form="♂ (male)"]
  Sensor_1 = male pin header, 3 pins [form="♂ (male)"]
  Sensor_2 = male pin header, 3 pins [form="♂ (male)"]
  Sensor_3 = male pin header, 3 pins [form="♂ (male)"]
  +_-_2 = male pin header, 2 pins [form="♂ (male)"]
  10kΩ = Resistor [tolerance=±5% resistance=10k package=THT]
  10kΩ_2 = Resistor [tolerance=±5% resistance=10k package=THT]
  10kΩ_3 = Resistor [tolerance=±5% resistance=10k package=THT]
  J13 = RPi GPIO Pins - 40 pins [form="♂ (shrouded male)" package=THT]
  Serial = male pin header, 2 pins [form="♂ (male)"]

nets:
  N1: Motor_1.pin1, J13.pin11
  N2: Motor_1.pin2, J13.pin13
  N3: Motor_1.pin3, J13.pin12
  N4: Motor_1.pin4, J13.pin16
  N5: Motor_2.pin1, J13.pin18
  N6: Motor_2.pin2, J13.pin22
  N7: Motor_2.pin3, J13.pin24
  N8: Motor_2.pin4, J13.pin26
  N9: Motor_3.pin1, J13.pin32
  N10: Motor_3.pin2, J13.pin36
  N11: Motor_3.pin3, J13.pin38
  N12: Motor_3.pin4, J13.pin40
  N13: J7.pin1, +_-.pin1, +_-_2.pin1, J13.pin6
  N14: J7.pin2, +_-.pin2, +_-_2.pin2, J13.pin4
  N15: Sensor_1.pin1, Sensor_2.pin1, Sensor_3.pin1, 10kΩ.Pin_0, 10kΩ_2.Pin_0, 10kΩ_3.Pin_0, J13.pin1
  N16: Sensor_1.pin2, Sensor_2.pin2, Sensor_3.pin2, J13.pin9
  N17: Sensor_1.pin3, 10kΩ.Pin_1, J13.pin33
  N18: Sensor_2.pin3, 10kΩ_2.Pin_1, J13.pin35
  N19: Sensor_3.pin3, 10kΩ_3.Pin_1, J13.pin37
  N20: J13.pin10, Serial.pin2
  N21: J13.pin8, Serial.pin1

custom parts:
  RPi GPIO Pins - 40 pins: Shrouded header for Raspberry Pi GPIO pinout
